# Fritzing sketch sketch (saved by Fritzing 0.9.2b)

parts:
  Raspberry_Pi2 = Raspberry Pi B+
  Q1 = NPN-Transistor [package="SOT-23 [SMD]"]
  Q2 = NPN-Transistor [package="SOT-23 [SMD]"]
  R1 = Resistor [tolerance=±5% resistance=4.7k package=THT]
  R2 = Resistor [tolerance=±5% resistance=4.7k package=THT]
  JP1 = Header 4 [part_number=FAN package=jst-4-pth]
  JP2 = Header 4 [part_number=LIGHT package=jst-4-pth]
  J1 = Power Jack [package=power_jack_pth]
  RHT1 = Humidity and Temperature Sensor RHT03
  U1 = Voltage Regulator [part_number="FPV BEC" package=to-220-alt]

nets:
  3V3: Raspberry_Pi2.3v3, Raspberry_Pi2.3V3, RHT1.Vcc
  N1: Raspberry_Pi2.GPIO4, RHT1.Data-signal
  GND: Raspberry_Pi2.GND, Q1.2, Q2.2, J1.GND, J1.GNDBREAK, RHT1.GND_2, U1.GND
  N2: Raspberry_Pi2.GPIO27, R1.Pin_0
  N3: Raspberry_Pi2.GPIO22, R2.Pin_0
  N4: Raspberry_Pi2.5V, U1.OUT
  N5: Q1.0, R2.Pin_1
  N6: Q1.1, JP1.4
  N7: Q2.0, R1.Pin_1
  N8: Q2.1, JP2.4
  N9: JP1.1, JP2.1, J1.PWR, U1.IN
